// Logisim project pipelined with forwarding.circ as structural Verilog: 10 circuits, main circuit main
module main (
);

  wire button_1_out, clock_1_out, cpu_1_illegal, cpu_1_load, cpu_1_store;
  wire [2:0] cpu_1_memwidth;
  wire [23:0] cpu_1_pc;
  wire [31:0] cpu_1_memaddr, cpu_1_pc_2, cpu_1_storevalue, memory_1_loadvalue, rom_1_data;

  Clock clock_1 (.out(clock_1_out));
  Button button_1 (.out(button_1_out));
  // OR_Gate or_1 has open pins: in0=cpu_1_illegal, in1=clock_1_out, out=open
  CPU cpu_1 (
    .Instruction(rom_1_data), .LoadValue(memory_1_loadvalue), .Clock(clock_1_out), .Reset(button_1_out),
    .Illegal(cpu_1_illegal), .MemWidth(cpu_1_memwidth), .Store(cpu_1_store), .load(cpu_1_load),
    .MemAddr(cpu_1_memaddr), .StoreValue(cpu_1_storevalue),
    .PC({cpu_1_pc_2[31:26], cpu_1_pc, cpu_1_pc_2[1:0]}));
  ROM #(.addrWidth(24), .dataWidth(32)) rom_1 (.addr(cpu_1_pc), .data(rom_1_data));
  Memory memory_1 (
    .Width(cpu_1_memwidth), .Store(cpu_1_store), .Load(cpu_1_load), .Address(cpu_1_memaddr),
    .StoreValue(cpu_1_storevalue), .Clock(clock_1_out), .LoadValue(memory_1_loadvalue));

  // Notes on the sheet:
  //   contents of rom_1 (hex, n*v repeats v):
  //   800093 300113 2081b3 293 118233
endmodule

module Extractor (
  input  [31:0] Instruction,
  input  [2:0] Format,
  input  clock,
  input  reset,
  output [6:0] Opcode,
  output [4:0] WB_RD,
  output [2:0] Funct3,
  output [4:0] RS1,
  output [4:0] RS2,
  output [6:0] funct7,
  output [31:0] Immediate_EX,
  output [31:0] Immediate_WB,
  output [4:0] MEM_RD
);

  wire [4:0] ID_EX_RD_q;
  wire [31:0] EX_MEM_IMM_q, multiplexer_1_out;

  Register #(.width(3)) ID_EX_func3 (.D(Instruction[14:12]), .clk(clock), .Q(Funct3), .clr(reset));  // open: en
  Multiplexer #(.select(3), .width(32)) multiplexer_1 (
    .in1({{21{Instruction[31]}}, Instruction[30:20]}),
    .in2({{21{Instruction[31]}}, Instruction[30:25], Instruction[11:7]}),
    .in3({{20{Instruction[31]}}, Instruction[7], Instruction[30:25], Instruction[11:8], 1'b0}),
    .in4({Instruction[31:12], {12{1'b0}}}),
    .in5({{12{Instruction[31]}}, Instruction[19:12], Instruction[20], Instruction[30:21], 1'b0}),
    .in6({32{1'b0}}), .in7({32{1'b0}}), .out(multiplexer_1_out), .sel(Format));  // open: in0
  Register #(.width(5)) ID_EX_RD (.D(Instruction[11:7]), .clk(clock), .Q(ID_EX_RD_q), .clr(reset));  // open: en
  Register #(.width(7)) ID_EX_func7 (.D(Instruction[31:25]), .clk(clock), .Q(funct7), .clr(reset));  // open: en
  Register #(.width(32)) ID_EX_IMM (.D(multiplexer_1_out), .clk(clock), .Q(Immediate_EX), .clr(reset));  // open: en
  Register #(.width(5)) EX_MEM_RD (.D(ID_EX_RD_q), .clk(clock), .Q(MEM_RD), .clr(reset));  // open: en
  Register #(.width(32)) EX_MEM_IMM (.D(Immediate_EX), .clk(clock), .Q(EX_MEM_IMM_q));  // open: en, clr
  Register #(.width(32)) ME_WB_IMM (.D(EX_MEM_IMM_q), .clk(clock), .Q(Immediate_WB), .clr(reset));  // open: en
  Register #(.width(5)) MEM_WB_RD (.D(MEM_RD), .clk(clock), .Q(WB_RD), .clr(reset));  // open: en

  assign Opcode = Instruction[6:0];
  assign RS1 = Instruction[19:15];
  assign RS2 = Instruction[24:20];

  // Notes on the sheet:
  //   I-type
  //   S-type
  //   B-type
  //   U-type
  //   J-type
endmodule

module Registers16 (
  input  Write,
  input  [3:0] RD,
  input  Clock,
  input  [31:0] Data,
  input  [3:0] RS1,
  input  [3:0] RS2,
  output [31:0] Out1,
  output [31:0] Out2
);

  wire decoder_1_out0, decoder_1_out1, decoder_1_out2, decoder_1_out3, decoder_1_out4, decoder_1_out5,
       decoder_1_out6, decoder_1_out7, decoder_1_out8, decoder_1_out9, decoder_1_out10, decoder_1_out11,
       decoder_1_out12, decoder_1_out13, decoder_1_out14, decoder_1_out15;
  wire [31:0] register_1_q, register_2_q, register_3_q, register_4_q, register_5_q, register_6_q,
       register_7_q, register_8_q, register_9_q, register_10_q, register_11_q, register_12_q, register_13_q,
       register_14_q, register_15_q, register_16_q;

  Multiplexer #(.select(4), .width(32)) multiplexer_1 (
    .in0(register_1_q), .in1(register_2_q), .in2(register_3_q), .in3(register_4_q), .in4(register_5_q),
    .in5(register_6_q), .in6(register_7_q), .in7(register_8_q), .in8(register_9_q), .in9(register_10_q),
    .in10(register_11_q), .in11(register_12_q), .in12(register_13_q), .in13(register_14_q),
    .in14(register_15_q), .in15(register_16_q), .out(Out1), .sel(RS1));
  Multiplexer #(.select(4), .width(32)) multiplexer_2 (
    .in0(register_1_q), .in1(register_2_q), .in2(register_3_q), .in3(register_4_q), .in4(register_5_q),
    .in5(register_6_q), .in6(register_7_q), .in7(register_8_q), .in8(register_9_q), .in9(register_10_q),
    .in10(register_11_q), .in11(register_12_q), .in12(register_13_q), .in13(register_14_q),
    .in14(register_15_q), .in15(register_16_q), .out(Out2), .sel(RS2));
  Decoder #(.select(4)) decoder_1 (
    .out0(decoder_1_out0), .out1(decoder_1_out1), .out2(decoder_1_out2), .out3(decoder_1_out3),
    .out4(decoder_1_out4), .out5(decoder_1_out5), .out6(decoder_1_out6), .out7(decoder_1_out7),
    .out8(decoder_1_out8), .out9(decoder_1_out9), .out10(decoder_1_out10), .out11(decoder_1_out11),
    .out12(decoder_1_out12), .out13(decoder_1_out13), .out14(decoder_1_out14), .out15(decoder_1_out15),
    .sel(RD), .en(Write));
  Register #(.trigger("falling"), .width(32)) register_1 (
    .D(Data), .en(decoder_1_out0), .clk(Clock), .Q(register_1_q));  // open: clr
  Register #(.trigger("falling"), .width(32)) register_2 (
    .D(Data), .en(decoder_1_out1), .clk(Clock), .Q(register_2_q));  // open: clr
  Register #(.trigger("falling"), .width(32)) register_3 (
    .D(Data), .en(decoder_1_out2), .clk(Clock), .Q(register_3_q));  // open: clr
  Register #(.trigger("falling"), .width(32)) register_4 (
    .D(Data), .en(decoder_1_out3), .clk(Clock), .Q(register_4_q));  // open: clr
  Register #(.trigger("falling"), .width(32)) register_5 (
    .D(Data), .en(decoder_1_out4), .clk(Clock), .Q(register_5_q));  // open: clr
  Register #(.trigger("falling"), .width(32)) register_6 (
    .D(Data), .en(decoder_1_out5), .clk(Clock), .Q(register_6_q));  // open: clr
  Register #(.trigger("falling"), .width(32)) register_7 (
    .D(Data), .en(decoder_1_out6), .clk(Clock), .Q(register_7_q));  // open: clr
  Register #(.trigger("falling"), .width(32)) register_8 (
    .D(Data), .en(decoder_1_out7), .clk(Clock), .Q(register_8_q));  // open: clr
  Register #(.trigger("falling"), .width(32)) register_9 (
    .D(Data), .en(decoder_1_out8), .clk(Clock), .Q(register_9_q));  // open: clr
  Register #(.trigger("falling"), .width(32)) register_10 (
    .D(Data), .en(decoder_1_out9), .clk(Clock), .Q(register_10_q));  // open: clr
  Register #(.trigger("falling"), .width(32)) register_11 (
    .D(Data), .en(decoder_1_out10), .clk(Clock), .Q(register_11_q));  // open: clr
  Register #(.trigger("falling"), .width(32)) register_12 (
    .D(Data), .en(decoder_1_out11), .clk(Clock), .Q(register_12_q));  // open: clr
  Register #(.trigger("falling"), .width(32)) register_13 (
    .D(Data), .en(decoder_1_out12), .clk(Clock), .Q(register_13_q));  // open: clr
  Register #(.trigger("falling"), .width(32)) register_14 (
    .D(Data), .en(decoder_1_out13), .clk(Clock), .Q(register_14_q));  // open: clr
  Register #(.trigger("falling"), .width(32)) register_15 (
    .D(Data), .en(decoder_1_out14), .clk(Clock), .Q(register_15_q));  // open: clr
  Register #(.trigger("falling"), .width(32)) register_16 (
    .D(Data), .en(decoder_1_out15), .clk(Clock), .Q(register_16_q));  // open: clr
endmodule

module Registers16WithZero (
  input  Write,
  input  [3:0] RD,
  input  Clock,
  input  [31:0] Data,
  input  [3:0] RS1,
  input  [3:0] RS2,
  output [31:0] Out1,
  output [31:0] Out2
);

  wire decoder_1_out1, decoder_1_out2, decoder_1_out3, decoder_1_out4, decoder_1_out5, decoder_1_out6,
       decoder_1_out7, decoder_1_out8, decoder_1_out9, decoder_1_out10, decoder_1_out11, decoder_1_out12,
       decoder_1_out13, decoder_1_out14, decoder_1_out15;
  wire [31:0] register_1_q, register_2_q, register_3_q, register_4_q, register_5_q, register_6_q,
       register_7_q, register_8_q, register_9_q, register_10_q, register_11_q, register_12_q, register_13_q,
       register_14_q, register_15_q;

  Multiplexer #(.select(4), .width(32)) multiplexer_1 (
    .in0({32{1'b0}}), .in1(register_1_q), .in2(register_2_q), .in3(register_3_q), .in4(register_4_q),
    .in5(register_5_q), .in6(register_6_q), .in7(register_7_q), .in8(register_8_q), .in9(register_9_q),
    .in10(register_10_q), .in11(register_11_q), .in12(register_12_q), .in13(register_13_q),
    .in14(register_14_q), .in15(register_15_q), .out(Out1), .sel(RS1));
  Multiplexer #(.select(4), .width(32)) multiplexer_2 (
    .in0({32{1'b0}}), .in1(register_1_q), .in2(register_2_q), .in3(register_3_q), .in4(register_4_q),
    .in5(register_5_q), .in6(register_6_q), .in7(register_7_q), .in8(register_8_q), .in9(register_9_q),
    .in10(register_10_q), .in11(register_11_q), .in12(register_12_q), .in13(register_13_q),
    .in14(register_14_q), .in15(register_15_q), .out(Out2), .sel(RS2));
  Decoder #(.select(4)) decoder_1 (
    .out1(decoder_1_out1), .out2(decoder_1_out2), .out3(decoder_1_out3), .out4(decoder_1_out4),
    .out5(decoder_1_out5), .out6(decoder_1_out6), .out7(decoder_1_out7), .out8(decoder_1_out8),
    .out9(decoder_1_out9), .out10(decoder_1_out10), .out11(decoder_1_out11), .out12(decoder_1_out12),
    .out13(decoder_1_out13), .out14(decoder_1_out14), .out15(decoder_1_out15), .sel(RD), .en(Write));  // open: out0
  Register #(.trigger("falling"), .width(32)) register_1 (
    .D(Data), .en(decoder_1_out1), .clk(Clock), .Q(register_1_q));  // open: clr
  Register #(.trigger("falling"), .width(32)) register_2 (
    .D(Data), .en(decoder_1_out2), .clk(Clock), .Q(register_2_q));  // open: clr
  Register #(.trigger("falling"), .width(32)) register_3 (
    .D(Data), .en(decoder_1_out3), .clk(Clock), .Q(register_3_q));  // open: clr
  Register #(.trigger("falling"), .width(32)) register_4 (
    .D(Data), .en(decoder_1_out4), .clk(Clock), .Q(register_4_q));  // open: clr
  Register #(.trigger("falling"), .width(32)) register_5 (
    .D(Data), .en(decoder_1_out5), .clk(Clock), .Q(register_5_q));  // open: clr
  Register #(.trigger("falling"), .width(32)) register_6 (
    .D(Data), .en(decoder_1_out6), .clk(Clock), .Q(register_6_q));  // open: clr
  Register #(.trigger("falling"), .width(32)) register_7 (
    .D(Data), .en(decoder_1_out7), .clk(Clock), .Q(register_7_q));  // open: clr
  Register #(.trigger("falling"), .width(32)) register_8 (
    .D(Data), .en(decoder_1_out8), .clk(Clock), .Q(register_8_q));  // open: clr
  Register #(.trigger("falling"), .width(32)) register_9 (
    .D(Data), .en(decoder_1_out9), .clk(Clock), .Q(register_9_q));  // open: clr
  Register #(.trigger("falling"), .width(32)) register_10 (
    .D(Data), .en(decoder_1_out10), .clk(Clock), .Q(register_10_q));  // open: clr
  Register #(.trigger("falling"), .width(32)) register_11 (
    .D(Data), .en(decoder_1_out11), .clk(Clock), .Q(register_11_q));  // open: clr
  Register #(.trigger("falling"), .width(32)) register_12 (
    .D(Data), .en(decoder_1_out12), .clk(Clock), .Q(register_12_q));  // open: clr
  Register #(.trigger("falling"), .width(32)) register_13 (
    .D(Data), .en(decoder_1_out13), .clk(Clock), .Q(register_13_q));  // open: clr
  Register #(.trigger("falling"), .width(32)) register_14 (
    .D(Data), .en(decoder_1_out14), .clk(Clock), .Q(register_14_q));  // open: clr
  Register #(.trigger("falling"), .width(32)) register_15 (
    .D(Data), .en(decoder_1_out15), .clk(Clock), .Q(register_15_q));  // open: clr

  // Notes on the sheet:
  //   ZERO
  //   RA
  //   SP
  //   GP
  //   TP
  //   T0
  //   T1
  //   T2
  //   S0
  //   S1
  //   A0
  //   A1
  //   S2
  //   S3
  //   S4
  //   S5
endmodule

module RegisterFile (
  input  [31:0] Data,
  input  [4:0] RD,
  input  Write,
  input  Clock,
  input  [4:0] RS1,
  input  [4:0] RS2,
  input  reset,
  output [31:0] Out1,
  output [31:0] Out2,
  output [4:0] EX_Rs1,
  output [4:0] EX_Rs2,
  output MEM_RegWrite,
  output WB_RegWrite
);

  wire demultiplexer_1_out0, demultiplexer_1_out1, ID_EX_RegWrite_q;
  wire [31:0] BottomRegisters_out1, BottomRegisters_out2, multiplexer_1_out, multiplexer_2_out,
       TopRegisters_out1, TopRegisters_out2;

  Register #(.width(1)) ID_EX_RegWrite (.D(Write), .clk(Clock), .Q(ID_EX_RegWrite_q), .clr(reset));  // open: en
  Register #(.width(1)) EX_MEM_RegWrite (.D(ID_EX_RegWrite_q), .clk(Clock), .Q(MEM_RegWrite), .clr(reset));  // open: en
  Register #(.width(1)) MEM_WB_RegWrite (.D(MEM_RegWrite), .clk(Clock), .Q(WB_RegWrite), .clr(reset));  // open: en
  Demultiplexer demultiplexer_1 (
    .out0(demultiplexer_1_out0), .out1(demultiplexer_1_out1), .in(WB_RegWrite), .sel(RD[4]));
  Register #(.width(5)) ID_EX_Rs1 (.D(RS1), .clk(Clock), .Q(EX_Rs1), .clr(reset));  // open: en
  Register #(.width(5)) ID_EX_Rs2 (.D(RS2), .clk(Clock), .Q(EX_Rs2), .clr(reset));  // open: en
  Registers16WithZero BottomRegisters (
    .Write(demultiplexer_1_out0), .RD(RD[3:0]), .Clock(Clock), .Data(Data), .RS1(RS1[3:0]), .RS2(RS2[3:0]),
    .Out1(BottomRegisters_out1), .Out2(BottomRegisters_out2));
  Registers16 TopRegisters (
    .Write(demultiplexer_1_out1), .RD(RD[3:0]), .Clock(Clock), .Data(Data), .RS1(RS1[3:0]), .RS2(RS2[3:0]),
    .Out1(TopRegisters_out1), .Out2(TopRegisters_out2));
  Multiplexer #(.width(32)) multiplexer_1 (
    .in0(BottomRegisters_out1), .in1(TopRegisters_out1), .out(multiplexer_1_out), .sel(RS1[4]));
  Multiplexer #(.width(32)) multiplexer_2 (
    .in0(BottomRegisters_out2), .in1(TopRegisters_out2), .out(multiplexer_2_out), .sel(RS2[4]));
  Register #(.width(32)) ID_EX_OUT1 (.D(multiplexer_1_out), .clk(Clock), .Q(Out1), .clr(reset));  // open: en
  Register #(.width(32)) ID_EX_OUT2 (.D(multiplexer_2_out), .clk(Clock), .Q(Out2), .clr(reset));  // open: en
endmodule

module CPU (
  input  [31:0] Instruction,
  input  [31:0] LoadValue,
  input  Clock,
  input  Reset,
  output Illegal,
  output [2:0] MemWidth,
  output Store,
  output load,
  output [31:0] MemAddr,
  output [31:0] StoreValue,
  output [31:0] PC
);

  wire ALUOutEnable_EtoMem, and_1_out, branchunit_1_branch, decoder_1_out0, decoder_1_out3, decoder_1_out4,
       decoder_1_out5, decoder_1_out8, decoder_1_out12, decoder_1_out13, decoder_1_out24, decoder_1_out25,
       decoder_1_out27, EX_MEM_ALUOutEnable_q, EX_MEM_AUIPCToReg_q, EX_MEM_q, EX_MEM_StorePC_sel1_q,
       EX_MEM_StorePC_sel2_q, EX_StorePC_Sel1_q, EX_StorePC_Sel2_q, ID_EX_AUIPCToReg_q, ID_EX_Jump_q,
       ID_EX_MemRead_q, Imm_regEnable, MEM_RegWrite_OUT, MEM_WB_AUIPCToReg_q, MEM_WB_StorePC_sel1_q,
       MEM_WB_StorePC_sel2_q, nand_1_out, not_1_out, or_2_out, or_3_out, or_4_out, or_6_out, or_7_out,
       priority_encoder_1_p2, priority_encoder_1_p7, register_2_q, register_5_q, register_6_q, register_7_q,
       register_9_q, register_12_q, WB_RegWrite_OUT;
  wire [1:0] extractor_1_opcode, forwardingunit_1_forwarda, forwardingunit_1_forwardb;
  wire [2:0] priority_encoder_1_p5;
  wire [4:0] EX_RS1_OUT, EX_RS2_OUT, extractor_1_opcode_2, extractor_1_rs1, extractor_1_rs2, MEM_RD_OUT,
       WB_RD_OUT;
  wire [6:0] extractor_1_funct7;
  wire [31:0] adder_1_out, adder_2_out, adder_3_out, adder_4_out, alu_1_data, controlled_buffer_1_out,
       extractor_1_immediate_ex, extractor_1_immediate_wb, ID_EX_PC_q, IF_ID_INST_q, IF_ID_PC_q, IN_A, IN_B,
       MEM_ALUOUT, MEM_WB_ALUOUT, MEM_WB_MemData_q, multiplexer_1_out, multiplexer_2_out, OUT1_Mux, OUT2_Mux,
       register_3_q, register_4_q, registerfile_1_out2;

  Register #(.width(32)) IF_ID_INST (.D(Instruction), .clk(Clock), .Q(IF_ID_INST_q), .clr(Reset));  // open: en
  Register #(.trigger("falling"), .width(32)) register_1 (
    .D(multiplexer_1_out), .clk(Clock), .Q(PC), .clr(Reset));  // open: en
  Decoder #(.select(5)) decoder_1 (
    .out0(decoder_1_out0), .out3(decoder_1_out3), .out4(decoder_1_out4), .out5(decoder_1_out5),
    .out8(decoder_1_out8), .out12(decoder_1_out12), .out13(decoder_1_out13), .out24(decoder_1_out24),
    .out25(decoder_1_out25), .out27(decoder_1_out27), .sel(extractor_1_opcode_2));  // open: out1, out2, out6, out7, out9, out10, out11, out14, out15, out16, out17, out18, out19, out20, out21, out22, out23, out26, out28, out29, out30, out31, en
  Multiplexer #(.width(32)) multiplexer_1 (
    .in0(adder_2_out), .in1(adder_4_out), .out(multiplexer_1_out), .sel(EX_StorePC_Sel1_q));
  Extractor extractor_1 (
    .Instruction(IF_ID_INST_q), .Format(priority_encoder_1_p5), .clock(Clock), .reset(Reset),
    .Opcode({extractor_1_opcode_2, extractor_1_opcode}), .WB_RD(WB_RD_OUT), .Funct3(MemWidth),
    .RS1(extractor_1_rs1), .RS2(extractor_1_rs2), .funct7(extractor_1_funct7),
    .Immediate_EX(extractor_1_immediate_ex), .Immediate_WB(extractor_1_immediate_wb), .MEM_RD(MEM_RD_OUT));
  Register #(.width(32)) IF_ID_PC (.D(PC), .clk(Clock), .Q(IF_ID_PC_q), .clr(Reset));  // open: en
  or or_1 (Illegal, nand_1_out, not_1_out);
  nand nand_1 (nand_1_out, extractor_1_opcode[1], extractor_1_opcode[0]);
  Adder #(.width(32)) adder_1 (.a(ID_EX_PC_q), .b(extractor_1_immediate_wb), .out(adder_1_out));  // open: cin, cout
  Adder #(.width(32)) adder_2 (.a(ID_EX_PC_q), .b(multiplexer_2_out), .out(adder_2_out));  // open: cin, cout
  Adder #(.width(32)) adder_3 (.a(ID_EX_PC_q), .b(32'h4), .out(adder_3_out));  // open: cin, cout
  not not_1 (not_1_out, register_2_q);
  assign controlled_buffer_1_out = MEM_WB_AUIPCToReg_q ? adder_1_out : 32'bz;  // Controlled_Buffer controlled_buffer_1
  Register #(.width(1)) register_2 (.D(priority_encoder_1_p7), .clk(Clock), .Q(register_2_q), .clr(Reset));  // open: en
  Multiplexer #(.width(32)) multiplexer_2 (
    .in0(32'h4), .in1(extractor_1_immediate_ex), .out(multiplexer_2_out), .sel(or_4_out));
  assign controlled_buffer_1_out = or_2_out ? register_4_q : 32'bz;  // Controlled_Buffer controlled_buffer_2
  Register #(.width(32)) ID_EX_PC (.D(IF_ID_PC_q), .clk(Clock), .Q(ID_EX_PC_q), .clr(Reset));  // open: en
  RegisterFile registerfile_1 (
    .Data(controlled_buffer_1_out), .RD(WB_RD_OUT), .Write(or_6_out), .Clock(Clock), .RS1(extractor_1_rs1),
    .RS2(extractor_1_rs2), .reset(Reset), .Out1(OUT1_Mux), .Out2(registerfile_1_out2), .EX_Rs1(EX_RS1_OUT),
    .EX_Rs2(EX_RS2_OUT), .MEM_RegWrite(MEM_RegWrite_OUT), .WB_RegWrite(WB_RegWrite_OUT));
  or or_2 (or_2_out, MEM_WB_StorePC_sel2_q, MEM_WB_StorePC_sel1_q);
  Register #(.width(32)) register_3 (.D(adder_3_out), .clk(Clock), .Q(register_3_q), .clr(Reset));  // open: en
  or or_3 (or_3_out, decoder_1_out13, decoder_1_out5);
  // Priority_Encoder priority_encoder_1: pin names not known; wires that end beside it: decoder_1_out12, priority_encoder_1_p2, decoder_1_out8, decoder_1_out24, priority_encoder_1_p5, or_3_out, priority_encoder_1_p7, decoder_1_out27, 1'b0, 1'b0, decoder_1_out3, decoder_1_out4, decoder_1_out0, decoder_1_out25
  assign controlled_buffer_1_out = Imm_regEnable ? extractor_1_immediate_wb : 32'bz;  // Controlled_Buffer controlled_buffer_3
  or or_4 (or_4_out, and_1_out, EX_StorePC_Sel2_q);
  or or_5 (priority_encoder_1_p2, decoder_1_out4, decoder_1_out0);
  Multiplexer #(.width(32)) multiplexer_3 (
    .in0(registerfile_1_out2), .in1(extractor_1_immediate_ex), .out(OUT2_Mux), .sel(register_5_q));
  Adder #(.width(32)) adder_4 (.a(OUT1_Mux), .b(extractor_1_immediate_ex), .out(adder_4_out));  // open: cin, cout
  Register #(.width(32)) register_4 (.D(register_3_q), .clk(Clock), .Q(register_4_q), .clr(Reset));  // open: en
  Register #(.width(1)) register_5 (.D(decoder_1_out4), .clk(Clock), .Q(register_5_q), .clr(Reset));  // open: en
  and and_1 (and_1_out, branchunit_1_branch, ID_EX_Jump_q);
  or or_6 (or_6_out, decoder_1_out25, decoder_1_out27, decoder_1_out0, decoder_1_out13, decoder_1_out5, decoder_1_out12, decoder_1_out4);
  or or_7 (or_7_out, decoder_1_out12, decoder_1_out4);
  Register #(.width(1)) register_6 (.D(or_7_out), .clk(Clock), .Q(register_6_q), .clr(Reset));  // open: en
  Register #(.width(1)) register_7 (.D(decoder_1_out13), .clk(Clock), .Q(register_7_q), .clr(Reset));  // open: en
  ForwardingUnit forwardingunit_1 (
    .ID_EX_rs1(EX_RS1_OUT), .ID_EX_rs2(EX_RS2_OUT), .EX_MEM_rd(MEM_RD_OUT), .MEM_WB_rd(WB_RD_OUT),
    .EX_MEM_RegWrite(MEM_RegWrite_OUT), .MEM_WB_RegWrite(WB_RegWrite_OUT),
    .ForwardA(forwardingunit_1_forwarda), .ForwardB(forwardingunit_1_forwardb));
  BranchUnit branchunit_1 (.A(OUT1_Mux), .B(OUT2_Mux), .Funct3(MemWidth), .Branch(branchunit_1_branch));
  Register #(.width(1)) ID_EX_Jump (.D(decoder_1_out24), .clk(Clock), .Q(ID_EX_Jump_q), .clr(Reset));  // open: en
  Register #(.width(32)) register_8 (.D(OUT2_Mux), .clk(Clock), .Q(StoreValue), .clr(Reset));  // open: en
  ALU alu_1 (.A(IN_A), .B(IN_B), .Funct3(MemWidth), .funct7(extractor_1_funct7), .Imm(register_5_q), .Data(alu_1_data));
  Multiplexer #(.select(2), .width(32)) multiplexer_4 (
    .in0(OUT1_Mux), .in1(MEM_ALUOUT), .in2(MEM_WB_ALUOUT), .out(IN_A));  // open: in3, sel
  Multiplexer #(.select(2), .width(32)) multiplexer_5 (
    .in0(OUT2_Mux), .in1(MEM_ALUOUT), .in2(MEM_WB_ALUOUT), .out(IN_B), .sel(forwardingunit_1_forwardb));  // open: in3
  Adder #(.width(32)) adder_5 (.a(OUT1_Mux), .b(extractor_1_immediate_ex), .out(MemAddr));  // open: cin, cout
  Register #(.width(1)) ID_EX_AUIPCToReg (
    .D(decoder_1_out5), .clk(Clock), .Q(ID_EX_AUIPCToReg_q), .clr(Reset));  // open: en
  Register #(.width(1)) EX_StorePC_Sel2 (
    .D(decoder_1_out27), .clk(Clock), .Q(EX_StorePC_Sel2_q), .clr(Reset));  // open: en
  Register #(.width(1)) EX_StorePC_Sel1 (
    .D(decoder_1_out25), .clk(Clock), .Q(EX_StorePC_Sel1_q), .clr(Reset));  // open: en
  Register #(.width(32)) MEM_WB_MemData (.D(LoadValue), .clk(Clock), .Q(MEM_WB_MemData_q), .clr(Reset));  // open: en
  Register #(.width(1)) register_9 (.D(decoder_1_out8), .clk(Clock), .Q(register_9_q), .clr(Reset));  // open: en
  Register #(.width(1)) EX_MEM_AUIPCToReg (
    .D(ID_EX_AUIPCToReg_q), .clk(Clock), .Q(EX_MEM_AUIPCToReg_q), .clr(Reset));  // open: en
  Register #(.width(1)) EX_MEM_StorePC_sel2 (
    .D(EX_StorePC_Sel2_q), .clk(Clock), .Q(EX_MEM_StorePC_sel2_q), .clr(Reset));  // open: en
  Register #(.width(1)) EX_MEM_StorePC_sel1 (
    .D(EX_StorePC_Sel1_q), .clk(Clock), .Q(EX_MEM_StorePC_sel1_q), .clr(Reset));  // open: en
  Register #(.width(1)) register_10 (.D(register_9_q), .clk(Clock), .Q(Store), .clr(Reset));  // open: en
  assign controlled_buffer_1_out = ALUOutEnable_EtoMem ? MEM_WB_ALUOUT : 32'bz;  // Controlled_Buffer controlled_buffer_4
  Register #(.width(1)) ID_EX_MemRead (.D(decoder_1_out0), .clk(Clock), .Q(ID_EX_MemRead_q), .clr(Reset));  // open: en
  Register #(.width(1)) MEM_WB_StorePC_sel1 (
    .D(EX_MEM_StorePC_sel1_q), .clk(Clock), .Q(MEM_WB_StorePC_sel1_q), .clr(Reset));  // open: en
  assign controlled_buffer_1_out = register_12_q ? MEM_WB_MemData_q : 32'bz;  // Controlled_Buffer controlled_buffer_5
  Register #(.width(1)) MEM_WB_AUIPCToReg (
    .D(EX_MEM_AUIPCToReg_q), .clk(Clock), .Q(MEM_WB_AUIPCToReg_q), .clr(Reset));  // open: en
  Register #(.width(1)) MEM_WB_StorePC_sel2 (
    .D(EX_MEM_StorePC_sel2_q), .clk(Clock), .Q(MEM_WB_StorePC_sel2_q), .clr(Reset));  // open: en
  Register #(.width(1)) register_11 (.D(ID_EX_MemRead_q), .clk(Clock), .Q(load), .clr(Reset));  // open: en
  Register #(.width(1)) register_12 (.D(load), .clk(Clock), .Q(register_12_q), .clr(Reset));  // open: en
  Register #(.width(32)) EX_MEM_ALU_Out (.D(alu_1_data), .clk(Clock), .Q(MEM_ALUOUT), .clr(Reset));  // open: en
  Register #(.width(1)) EX_MEM_ALUOutEnable (
    .D(register_6_q), .clk(Clock), .Q(EX_MEM_ALUOutEnable_q), .clr(Reset));  // open: en
  Register #(.width(1)) EX_MEM (.D(register_7_q), .clk(Clock), .Q(EX_MEM_q), .clr(Reset));  // open: en
  Register #(.width(1)) MEM_WB (.D(EX_MEM_q), .clk(Clock), .Q(Imm_regEnable), .clr(Reset));  // open: en
  Register #(.width(32)) u_MEM_WB_ALUOut (.D(MEM_ALUOUT), .clk(Clock), .Q(MEM_WB_ALUOUT), .clr(Reset));  // open: en
  Register #(.width(1)) MEM_WB_ALUOutEnable (
    .D(EX_MEM_ALUOutEnable_q), .clk(Clock), .Q(ALUOutEnable_EtoMem), .clr(Reset));  // open: en

  // Notes on the sheet:
  //   AUIPC
  //   Store PC?
endmodule

module ALU (
  input  [31:0] A,
  input  [31:0] B,
  input  [2:0] Funct3,
  input  [6:0] funct7,
  input  Imm,
  output [31:0] Data
);

  wire and_2_out, and_3_out, not_1_out;
  wire [0:0] comparator_1_lt, comparator_2_lt;
  wire [31:0] adder_1_out, and_1_out, divider_1_out, divider_1_rem, divider_2_out, divider_2_rem,
       multiplexer_1_out, multiplexer_2_out, multiplexer_3_out, multiplexer_4_out, multiplexer_6_out,
       negator_1_out, or_1_out, shifter_1_out, shifter_2_out, shifter_3_out, subtractor_1_out, xor_1_out;
  wire [63:0] multiplier_1_out, multiplier_2_out, multiplier_3_out, negator_2_out;

  not not_1 (not_1_out, Imm);
  assign xor_1_out = A ^ B;  // XOR_Gate xor_1, 32 bits wide
  assign or_1_out = A | B;  // OR_Gate or_1, 32 bits wide
  assign and_1_out = A & B;  // AND_Gate and_1, 32 bits wide
  Shifter #(.width(32)) shifter_1 (.in(A), .\dist (B[4:0]), .out(shifter_1_out));
  Shifter #(.shift("lr"), .width(32)) shifter_2 (.in(A), .\dist (B[4:0]), .out(shifter_2_out));
  Shifter #(.shift("ar"), .width(32)) shifter_3 (.in(A), .\dist (B[4:0]), .out(shifter_3_out));
  Negator #(.width(32)) negator_1 (.in(B), .out(negator_1_out));
  Adder #(.width(32)) adder_1 (.a(A), .b(B), .out(adder_1_out));  // open: cin, cout
  Subtractor #(.width(32)) subtractor_1 (.a(A), .b(B), .out(subtractor_1_out));  // open: bin, bout
  and and_2 (and_2_out, funct7[5], not_1_out);
  Comparator #(.width(32)) comparator_1 (.a(A), .b(B), .lt(comparator_1_lt[0]));  // open: gt, eq
  Comparator #(.mode("unsigned"), .width(32)) comparator_2 (.a(A), .b(B), .lt(comparator_2_lt[0]));  // open: gt, eq
  Multiplexer #(.width(32)) multiplexer_1 (
    .in0(shifter_2_out), .in1(shifter_3_out), .out(multiplexer_1_out), .sel(funct7[5]));
  Multiplexer #(.width(32)) multiplexer_2 (
    .in0(adder_1_out), .in1(subtractor_1_out), .out(multiplexer_2_out), .sel(and_2_out));
  Divider #(.width(32)) divider_1 (.a(A), .b(B), .out(divider_1_out), .rem(divider_1_rem));  // open: upper
  Divider #(.mode("twosComplement"), .width(32)) divider_2 (
    .a(A), .b(B), .out(divider_2_out), .rem(divider_2_rem));  // open: upper
  Multiplexer #(.select(3), .width(32)) multiplexer_3 (
    .in0(multiplier_3_out[31:0]), .in1(multiplier_3_out[63:32]), .in2(multiplexer_6_out),
    .in3(multiplier_2_out[63:32]), .in4(divider_2_out), .in5(divider_1_out), .in6(divider_2_rem),
    .in7(divider_1_rem), .out(multiplexer_3_out), .sel(Funct3));
  Multiplexer #(.select(3), .width(32)) multiplexer_4 (
    .in0(multiplexer_2_out), .in1(shifter_1_out), .in2({{31{1'b0}}, comparator_1_lt[0]}),
    .in3({{31{1'b0}}, comparator_2_lt[0]}), .in4(xor_1_out), .in5(multiplexer_1_out), .in6(or_1_out),
    .in7(and_1_out), .out(multiplexer_4_out), .sel(Funct3));
  Multiplier #(.width(64)) multiplier_1 (
    .a({{32{1'b0}}, negator_1_out}), .b({{32{1'b0}}, A}), .out(multiplier_1_out));  // open: cin, cout
  Multiplexer #(.width(32)) multiplexer_5 (
    .in0(multiplexer_4_out), .in1(multiplexer_3_out), .out(Data), .sel(and_3_out));
  and and_3 (and_3_out, funct7[0], ~Imm);  // AND_Gate
  Negator #(.width(64)) negator_2 (.in(multiplier_1_out), .out(negator_2_out));
  Multiplier #(.width(64)) multiplier_2 (
    .a({{32{1'b0}}, B}), .b({{32{1'b0}}, A}), .out(multiplier_2_out));  // open: cin, cout
  Multiplexer #(.width(32)) multiplexer_6 (
    .in0(negator_2_out[63:32]), .in1(multiplier_2_out[63:32]), .out(multiplexer_6_out),
    .sel(negator_1_out[31]));
  Multiplier #(.mode("twosComplement"), .width(64)) multiplier_3 (
    .a({{33{B[31]}}, B[30:0]}), .b({{33{A[31]}}, A[30:0]}), .out(multiplier_3_out));  // open: cin, cout
endmodule

module BranchUnit (
  input  [31:0] A,
  input  [31:0] B,
  input  [2:0] Funct3,
  output Branch
);

  wire comparator_1_eq, comparator_1_gt, comparator_1_lt, comparator_2_eq, comparator_2_gt, comparator_2_lt,
       not_1_out, or_1_out, or_2_out;

  Comparator #(.mode("unsigned"), .width(32)) comparator_1 (
    .a(A), .b(B), .gt(comparator_1_gt), .eq(comparator_1_eq), .lt(comparator_1_lt));
  Comparator #(.width(32)) comparator_2 (
    .a(A), .b(B), .gt(comparator_2_gt), .eq(comparator_2_eq), .lt(comparator_2_lt));
  not not_1 (not_1_out, comparator_1_eq);
  or or_1 (or_1_out, comparator_1_gt, comparator_1_eq);
  or or_2 (or_2_out, comparator_2_gt, comparator_2_eq);
  Multiplexer #(.select(3)) multiplexer_1 (
    .in0(comparator_1_eq), .in1(not_1_out), .in2(1'b0), .in3(1'b0), .in4(comparator_2_lt), .in5(or_2_out),
    .in6(comparator_1_lt), .in7(or_1_out), .out(Branch), .sel(Funct3));
endmodule

module Memory (
  input  [2:0] Width,
  input  Store,
  input  Load,
  input  [31:0] Address,
  input  [31:0] StoreValue,
  input  Clock,
  output [31:0] LoadValue
);

  wire not_1_out, not_2_out, not_3_out, not_4_out, or_1_out;
  wire [1:0] subtractor_1_out_2;
  wire [31:0] multiplexer_1_out, multiplexer_2_out, multiplexer_3_out, multiplexer_4_out, multiplexer_5_out,
       multiplexer_7_out, multiplexer_8_out, multiplexer_9_out, multiplexer_10_out, multiplexer_11_out,
       multiplexer_12_out, ram_1_dout, ram_1_dout_2;
  wire [31:2] subtractor_1_out;
  wire [31:8] ram_1_dout_3, ram_1_dout_4;

  Subtractor #(.width(32)) subtractor_1 (
    .a(Address), .b(32'h1000000), .out({subtractor_1_out, subtractor_1_out_2}));  // open: bin, bout
  or or_1 (or_1_out, Store, Load);
  Multiplexer #(.width(32)) multiplexer_1 (
    .in0({ram_1_dout_4[31], ram_1_dout_4[14:8], ram_1_dout_3[31], ram_1_dout_3[14:8], StoreValue[15:0]}),
    .in1({ram_1_dout_4[31], ram_1_dout_4[14:8], StoreValue[15:0], ram_1_dout[31], ram_1_dout[6:0]}),
    .out(multiplexer_1_out), .sel(subtractor_1_out_2[0]));
  Multiplexer #(.width(32)) multiplexer_2 (
    .in0(multiplexer_1_out),
    .in1({StoreValue[15:0], ram_1_dout_2[31], ram_1_dout_2[6:0], ram_1_dout[31], ram_1_dout[6:0]}),
    .out(multiplexer_2_out), .sel(subtractor_1_out_2[1]));
  Multiplexer #(.select(2), .width(32)) multiplexer_3 (
    .in0({ram_1_dout_4[31], ram_1_dout_4[14:8], ram_1_dout_3[31], ram_1_dout_3[14:8], ram_1_dout_2[31], ram_1_dout_2[6:0], StoreValue[7:0]}),
    .in1({ram_1_dout_4[31], ram_1_dout_4[14:8], ram_1_dout_3[31], ram_1_dout_3[14:8], StoreValue[7:0], ram_1_dout[31], ram_1_dout[6:0]}),
    .in2({ram_1_dout_4[31], ram_1_dout_4[14:8], StoreValue[7:0], ram_1_dout_2[31], ram_1_dout_2[6:0], ram_1_dout[31], ram_1_dout[6:0]}),
    .in3({StoreValue[7:0], ram_1_dout_3[31], ram_1_dout_3[14:8], ram_1_dout_2[31], ram_1_dout_2[6:0], ram_1_dout[31], ram_1_dout[6:0]}),
    .out(multiplexer_3_out), .sel(subtractor_1_out_2));
  Multiplexer #(.width(32)) multiplexer_4 (
    .in0(StoreValue), .in1(multiplexer_5_out), .out(multiplexer_4_out), .sel(not_1_out));
  not not_1 (not_1_out, Width[1]);
  not not_2 (not_2_out, Width[0]);
  Multiplexer #(.width(32)) multiplexer_5 (
    .in0(multiplexer_2_out), .in1(multiplexer_3_out), .out(multiplexer_5_out), .sel(not_2_out));
  RAM #(.addrWidth(24), .asyncread("true"), .dataWidth(32), .trigger("falling")) ram_1 (
    .addr(subtractor_1_out[25:2]), .we(Store), .oe(or_1_out), .clk(Clock), .din(multiplexer_4_out),
    .dout({ram_1_dout_4[31], ram_1_dout_4[14:8], ram_1_dout_3[31], ram_1_dout_3[14:8], ram_1_dout_2[31], ram_1_dout_2[6:0], ram_1_dout[31], ram_1_dout[6:0]}));
  Multiplexer #(.width(32)) multiplexer_6 (
    .in0({ram_1_dout_4[31], ram_1_dout_4[14:8], ram_1_dout_3[31], ram_1_dout_3[14:8], ram_1_dout_2[31], ram_1_dout_2[6:0], ram_1_dout[31], ram_1_dout[6:0]}),
    .in1(multiplexer_8_out), .out(LoadValue), .sel(not_3_out));
  not not_3 (not_3_out, Width[1]);
  not not_4 (not_4_out, Width[0]);
  Multiplexer #(.width(32)) multiplexer_7 (
    .in0({{17{ram_1_dout_2[31]}}, ram_1_dout_2[6:0], ram_1_dout[31], ram_1_dout[6:0]}),
    .in1({{17{ram_1_dout_3[31]}}, ram_1_dout_3[14:8], ram_1_dout_2[31], ram_1_dout_2[6:0]}),
    .out(multiplexer_7_out), .sel(subtractor_1_out_2[0]));
  Multiplexer #(.width(32)) multiplexer_8 (
    .in0(multiplexer_11_out), .in1(multiplexer_12_out), .out(multiplexer_8_out), .sel(not_4_out));
  Multiplexer #(.width(32)) multiplexer_9 (
    .in0(multiplexer_7_out),
    .in1({{17{ram_1_dout_4[31]}}, ram_1_dout_4[14:8], ram_1_dout_3[31], ram_1_dout_3[14:8]}),
    .out(multiplexer_9_out), .sel(subtractor_1_out_2[1]));
  Multiplexer #(.select(2), .width(32)) multiplexer_10 (
    .in0({{25{ram_1_dout[31]}}, ram_1_dout[6:0]}), .in1({{25{ram_1_dout_2[31]}}, ram_1_dout_2[6:0]}),
    .in2({{25{ram_1_dout_3[31]}}, ram_1_dout_3[14:8]}), .in3({{25{ram_1_dout_4[31]}}, ram_1_dout_4[14:8]}),
    .out(multiplexer_10_out), .sel(subtractor_1_out_2));
  Multiplexer #(.width(32)) multiplexer_11 (
    .in0(multiplexer_9_out), .in1({{16{1'b0}}, multiplexer_9_out[15:0]}), .out(multiplexer_11_out),
    .sel(Width[2]));
  Multiplexer #(.width(32)) multiplexer_12 (
    .in0(multiplexer_10_out), .in1({{24{1'b0}}, multiplexer_10_out[7:0]}), .out(multiplexer_12_out),
    .sel(Width[2]));
endmodule

module ForwardingUnit (
  input  [4:0] ID_EX_rs1,
  input  [4:0] ID_EX_rs2,
  input  [4:0] EX_MEM_rd,
  input  [4:0] MEM_WB_rd,
  input  EX_MEM_RegWrite,
  input  MEM_WB_RegWrite,
  output [1:0] ForwardA,
  output [1:0] ForwardB
);

  wire CMP1, CMP2, CMP3, CMP4, CMP5, CMP6, comparator_5_eq, comparator_6_eq, MEM_RS1_MATCH, MEM_RS2_MATCH,
       not_3_out, not_4_out;

  Comparator #(.mode("unsigned"), .width(5)) comparator_1 (.a(ID_EX_rs1), .b(EX_MEM_rd), .eq(CMP1));  // open: gt, lt
  Comparator #(.mode("unsigned"), .width(5)) comparator_2 (.a(ID_EX_rs2), .b(EX_MEM_rd), .eq(CMP2));  // open: gt, lt
  Comparator #(.mode("unsigned"), .width(5)) comparator_3 (.a(ID_EX_rs1), .b(MEM_WB_rd), .eq(CMP3));  // open: gt, lt
  Comparator #(.mode("unsigned"), .width(5)) comparator_4 (.a(ID_EX_rs2), .b(MEM_WB_rd), .eq(CMP4));  // open: gt, lt
  Comparator #(.mode("unsigned"), .width(5)) comparator_5 (
    .a(EX_MEM_rd), .b({5{1'b0}}), .eq(comparator_5_eq));  // open: gt, lt
  Comparator #(.mode("unsigned"), .width(5)) comparator_6 (
    .a(MEM_WB_rd), .b({5{1'b0}}), .eq(comparator_6_eq));  // open: gt, lt
  not not_1 (CMP5, comparator_5_eq);
  not not_2 (CMP6, comparator_6_eq);
  and and_1 (ForwardA[0], EX_MEM_RegWrite, CMP1, CMP5);
  and and_2 (ForwardB[0], EX_MEM_RegWrite, CMP2, CMP5);
  and and_3 (MEM_RS1_MATCH, MEM_WB_RegWrite, CMP3, CMP6);
  and and_4 (MEM_RS2_MATCH, MEM_WB_RegWrite, CMP4, CMP6);
  not not_3 (not_3_out, ForwardA[0]);
  not not_4 (not_4_out, ForwardB[0]);
  and and_5 (ForwardA[1], not_3_out, MEM_RS1_MATCH);
  and and_6 (ForwardB[1], not_4_out, MEM_RS2_MATCH);

  // Other names for the same wires on the sheet: EX_RS1_MATCH = ForwardA[0]; EX_RS2_MATCH = ForwardB[0];
  //   MEM_RegWrite = EX_MEM_RegWrite; WB_RegWrite = MEM_WB_RegWrite
endmodule
